// Logisim project schemes.circ as structural Verilog: 1 circuit, main circuit DataPath
module DataPath (
  input  in_1,
  input  in_2,
  input  in_3,
  input  in_4,
  input  in_5,
  input  in_6,
  input  in_7,
  input  in_8,
  input  in_9,
  input  in_10,
  input  in_11,
  input  in_12,
  input  in_13,
  input  in_14,
  input  in_15,
  input  in_16,
  input  [3:0] in_17
);

  wire [31:0] register_1_q, register_2_q, register_3_q, register_4_q, register_5_q, register_6_q,
       register_7_q, register_8_q, register_9_q, register_10_q, register_11_q, register_12_q, register_13_q,
       register_14_q, register_15_q, register_16_q;

  Register #(.width(32)) register_1 (.Q(register_1_q), .clk(in_1));  // open: D, en, clr
  Register #(.width(32)) register_2 (.Q(register_2_q), .clk(in_3));  // open: D, en, clr
  Register #(.width(32)) register_3 (.Q(register_3_q), .clk(in_5));  // open: D, en, clr
  Register #(.width(32)) register_4 (.Q(register_4_q), .clk(in_7));  // open: D, en, clr
  Register #(.width(32)) register_5 (.Q(register_5_q), .clk(in_9));  // open: D, en, clr
  Register #(.width(32)) register_6 (.Q(register_6_q), .clk(in_11));  // open: D, en, clr
  Register #(.width(32)) register_7 (.Q(register_7_q), .clk(in_13));  // open: D, en, clr
  Register #(.width(32)) register_8 (.Q(register_8_q), .clk(in_15));  // open: D, en, clr
  Register #(.width(32)) register_9 (.Q(register_9_q), .clk(in_2));  // open: D, en, clr
  Register #(.width(32)) register_10 (.Q(register_10_q), .clk(in_4));  // open: D, en, clr
  Register #(.width(32)) register_11 (.Q(register_11_q), .clk(in_6));  // open: D, en, clr
  Register #(.width(32)) register_12 (.Q(register_12_q), .clk(in_8));  // open: D, en, clr
  Register #(.width(32)) register_13 (.Q(register_13_q), .clk(in_10));  // open: D, en, clr
  Register #(.width(32)) register_14 (.Q(register_14_q), .clk(in_12));  // open: D, en, clr
  Register #(.width(32)) register_15 (.Q(register_15_q), .clk(in_14));  // open: D, en, clr
  Register #(.width(32)) register_16 (.Q(register_16_q), .clk(in_16));  // open: D, en, clr
  Multiplexer #(.select(4), .width(32)) multiplexer_1 (
    .in0(register_1_q), .in1(register_2_q), .in2(register_3_q), .in3(register_4_q), .in4(register_9_q),
    .in5(register_10_q), .in6(register_11_q), .in7(register_12_q), .in8(register_13_q), .in9(register_14_q),
    .in10(register_15_q), .in11(register_16_q), .in12(register_5_q), .in13(register_6_q),
    .in14(register_7_q), .in15(register_8_q), .sel(in_17));  // open: out, en
endmodule
